// Logisim project BLDIM.circ as structural Verilog
module PROCESSADOR (
);

  wire bolha_1_out_3, button_1_out, clock_1_out, UC_ld, UC_ra, UC_rw, UC_str, UC_wmd, ula_1_beq;
  wire [1:0] UC_ad, UC_ula_op, ula_end_1_end;
  wire [3:0] multiplexer_2_out;
  wire [31:0] adder_1_out, banco_de_registradores_1_r0_d, banco_de_registradores_1_r1_d,
       extensor_17_32_1_out_2, extensor_21_32_1_out_2, multiplexer_1_out, multiplexer_3_out, PC_q,
       ram_1_data, rom_1_data, ula_1_ula_out;

  Button button_1 (.out(button_1_out));
  BOLHA bolha_1 (.out_3(bolha_1_out_3), .INST(rom_1_data), .CLK(clock_1_out));
  Clock clock_1 (.out(clock_1_out));
  Adder #(.width(32)) adder_1 (.a(PC_q), .b(32'h1), .out(adder_1_out));  // open: cin, cout
  Multiplexer #(.select(2), .width(32)) multiplexer_1 (
    .in0(adder_1_out), .in1(extensor_21_32_1_out_2), .in2(banco_de_registradores_1_r1_d),
    .out(multiplexer_1_out), .sel(ula_end_1_end));  // open: in3, en
  ULA_END ula_end_1 (.END(ula_end_1_end), .ENDC(UC_ad), .EQUAL(ula_1_beq));
  Register #(.width(32)) PC (.D(multiplexer_1_out), .Q(PC_q), .clk(bolha_1_out_3), .clr(button_1_out));  // open: en
  EXTENSOR_21_32 extensor_21_32_1 (.in_1(rom_1_data[28:8]), .out_2(extensor_21_32_1_out_2));
  ROM #(.addrWidth(24), .dataWidth(32)) rom_1 (.addr(PC_q[23:0]), .data(rom_1_data));  // open: sel
  Multiplexer #(.width(4)) multiplexer_2 (
    .in0(rom_1_data[28:25]), .in1(4'b1111), .out(multiplexer_2_out), .sel(UC_ra));  // open: en
  UC UC (
    .E1(rom_1_data[31]), .E2(rom_1_data[30]), .E3(rom_1_data[29]), .RW(UC_rw), .ULA_OP(UC_ula_op),
    .STR(UC_str), .LD(UC_ld), .WMD(UC_wmd), .RA(UC_ra), .AD(UC_ad));
  BANCO_DE_REGISTRADORES banco_de_registradores_1 (
    .DATA_WRITE(multiplexer_3_out), .CLK(bolha_1_out_3), .RW(multiplexer_2_out),
    .R0_D(banco_de_registradores_1_r0_d), .R0(rom_1_data[7:4]), .R1_D(banco_de_registradores_1_r1_d),
    .R1(rom_1_data[3:0]), .RW_2(UC_rw), .RESET(button_1_out));
  EXTENSOR_17_32 extensor_17_32_1 (.in_1(rom_1_data[24:8]), .out_2(extensor_17_32_1_out_2));
  ULA ula_1 (
    .DATA_0(banco_de_registradores_1_r0_d), .DATA_1(banco_de_registradores_1_r1_d), .ULA_OUT(ula_1_ula_out),
    .ULA_OP(UC_ula_op), .IMEDIATO(extensor_17_32_1_out_2), .BEQ(ula_1_beq));
  RAM #(.dataWidth(32), .bus("separate")) ram_1 (
    .addr(ula_1_ula_out[7:0]), .din(banco_de_registradores_1_r1_d), .data(ram_1_data), .str(UC_str),
    .clk(bolha_1_out_3), .ld(UC_ld));  // open: sel, clr
  Multiplexer #(.width(32)) multiplexer_3 (
    .in0(ula_1_ula_out), .in1(ram_1_data), .out(multiplexer_3_out), .sel(UC_wmd));  // open: en

  // Notes on the sheet:
  //   contents of rom_1 (hex, n*v repeats v):
  //   2000100 14000000 16001000 1e002000 12000400 18000000 800023c9 1a000000 800021d9 4000000 1c000000
  //   2600019c 26000131 2800011d 80001ce9 2a00011e a0000a5 a000053 6c000050 2a00019e 2a000151 a0000b5
  //   a000054 6e000050 2c000167 4000026 1c0001e0 e0000e00 60000f3 6000034 40000032 1a0001d0 e0000800
  //   180001c0 e0000600
  //   REG_0
  //   REG_1
  //   REG_W
  //   DATA_W
  //   BLDIM
  //   Beautiful Loving Dear Impressive Micropocessor
  //   BANCO DE REGISTRADORES
  //   REG0_D
  //   REG1_D
  //   IMEDIATO
  //   ULA
endmodule

module ULA (
  input  [31:0] DATA_0,
  input  [31:0] DATA_1,
  input  [1:0] ULA_OP,
  input  [31:0] IMEDIATO,
  output [31:0] ULA_OUT,
  output BEQ
);

  wire [31:0] adder_1_out, adder_2_out, multiplier_1_out, multiplier_2_out;

  Adder #(.width(32)) adder_1 (.a(DATA_0), .b(DATA_1), .out(adder_1_out));  // open: cin, cout
  Adder #(.width(32)) adder_2 (.a(adder_1_out), .b(IMEDIATO), .out(adder_2_out));  // open: cin, cout
  Multiplier #(.width(32)) multiplier_1 (.a(DATA_0), .b(DATA_1), .out(multiplier_1_out));  // open: cin, cout
  Multiplier #(.width(32)) multiplier_2 (
    .a(multiplier_1_out), .b(IMEDIATO), .out(multiplier_2_out));  // open: cin, cout
  Comparator #(.width(32)) comparator_1 (.a(DATA_0), .b(DATA_1), .eq(BEQ));  // open: gt, lt
  Multiplexer #(.select(2), .width(32), .enable("false")) multiplexer_1 (
    .in0(adder_2_out), .in1(multiplier_2_out), .in3(DATA_0), .out(ULA_OUT), .sel(ULA_OP));  // open: in2
endmodule

module UC (
  input  E1,
  input  E2,
  input  E3,
  output RW,
  output [1:0] ULA_OP,
  output STR,
  output LD,
  output WMD,
  output RA,
  output [1:0] AD
);

  wire and_1_out, and_2_out, and_3_out, and_9_out, and_10_out, not_1_out, not_2_out, not_3_out, not_4_out,
       not_5_out, not_6_out, not_7_out, not_8_out, not_9_out, not_10_out, not_11_out;

  not not_1 (not_1_out, E1);
  not not_2 (not_2_out, E2);
  not not_3 (not_3_out, E1);
  not not_4 (not_4_out, E3);
  or or_1 (ULA_OP[1], E2, E1);
  or or_2 (ULA_OP[0], E3, E2);
  not not_5 (not_5_out, E1);
  not not_6 (not_6_out, E3);
  not not_7 (not_7_out, E1);
  not not_8 (not_8_out, E1);
  not not_9 (not_9_out, E3);
  not not_10 (not_10_out, E2);
  not not_11 (not_11_out, E3);
  and and_1 (and_1_out, not_1_out, not_2_out);
  and and_2 (and_2_out, not_3_out, E3);
  and and_3 (and_3_out, E1, E2, not_4_out);
  and and_4 (STR, not_5_out, E2, not_6_out);
  and and_5 (LD, not_7_out, E2, E3);
  and and_6 (WMD, not_8_out, E2, E3);
  and and_7 (RA, E1, E2, not_9_out);
  and and_8 (AD[1], E1, not_10_out);
  and and_9 (and_9_out, E1, not_11_out);
  and and_10 (and_10_out, E1, E2);
  or or_3 (RW, and_1_out, and_2_out, and_3_out);
  or or_4 (AD[0], and_9_out, and_10_out);
endmodule

module BANCO_DE_REGISTRADORES (
  input  [31:0] DATA_WRITE,
  input  [3:0] R0,
  input  CLK,
  input  [3:0] R1,
  input  [3:0] RW,
  input  RW_2,
  input  RESET,
  output [31:0] R0_D,
  output [31:0] R1_D
);

  wire demultiplexer_1_out0, demultiplexer_1_out1, demultiplexer_1_out2, demultiplexer_1_out3,
       demultiplexer_1_out4, demultiplexer_1_out5, demultiplexer_1_out6, demultiplexer_1_out7,
       demultiplexer_1_out8, demultiplexer_1_out9, demultiplexer_1_out10, demultiplexer_1_out11,
       demultiplexer_1_out12, demultiplexer_1_out13, demultiplexer_1_out14, demultiplexer_1_out15;
  wire [31:0] register_1_q, register_2_q, register_3_q, register_4_q, register_5_q, register_6_q,
       register_7_q, register_8_q, register_9_q, register_10_q, register_11_q, register_12_q, register_13_q,
       register_14_q, register_15_q, register_16_q;

  Demultiplexer #(.select(4), .enable("false")) demultiplexer_1 (
    .out0(demultiplexer_1_out0), .out1(demultiplexer_1_out1), .out2(demultiplexer_1_out2),
    .out3(demultiplexer_1_out3), .out4(demultiplexer_1_out4), .out5(demultiplexer_1_out5),
    .out6(demultiplexer_1_out6), .out7(demultiplexer_1_out7), .out8(demultiplexer_1_out8),
    .out9(demultiplexer_1_out9), .out10(demultiplexer_1_out10), .out11(demultiplexer_1_out11),
    .out12(demultiplexer_1_out12), .out13(demultiplexer_1_out13), .out14(demultiplexer_1_out14),
    .out15(demultiplexer_1_out15), .in(RW_2), .sel(RW));
  Register #(.width(32)) register_1 (
    .D(DATA_WRITE), .en(demultiplexer_1_out0), .Q(register_1_q), .clk(CLK), .clr(RESET));
  Register #(.width(32)) register_2 (
    .D(DATA_WRITE), .en(demultiplexer_1_out1), .Q(register_2_q), .clk(CLK), .clr(RESET));
  Register #(.width(32)) register_3 (
    .D(DATA_WRITE), .en(demultiplexer_1_out2), .Q(register_3_q), .clk(CLK), .clr(RESET));
  Register #(.width(32)) register_4 (
    .D(DATA_WRITE), .en(demultiplexer_1_out3), .Q(register_4_q), .clk(CLK), .clr(RESET));
  Register #(.width(32)) register_5 (
    .D(DATA_WRITE), .en(demultiplexer_1_out4), .Q(register_5_q), .clk(CLK), .clr(RESET));
  Register #(.width(32)) register_6 (
    .D(DATA_WRITE), .en(demultiplexer_1_out5), .Q(register_6_q), .clk(CLK), .clr(RESET));
  Register #(.width(32)) register_7 (
    .D(DATA_WRITE), .en(demultiplexer_1_out6), .Q(register_7_q), .clk(CLK), .clr(RESET));
  Register #(.width(32)) register_8 (
    .D(DATA_WRITE), .en(demultiplexer_1_out7), .Q(register_8_q), .clk(CLK), .clr(RESET));
  Register #(.width(32)) register_9 (
    .D(DATA_WRITE), .en(demultiplexer_1_out8), .Q(register_9_q), .clk(CLK), .clr(RESET));
  Register #(.width(32)) register_10 (
    .D(DATA_WRITE), .en(demultiplexer_1_out9), .Q(register_10_q), .clk(CLK), .clr(RESET));
  Register #(.width(32)) register_11 (
    .D(DATA_WRITE), .en(demultiplexer_1_out10), .Q(register_11_q), .clk(CLK), .clr(RESET));
  Register #(.width(32)) register_12 (
    .D(DATA_WRITE), .en(demultiplexer_1_out11), .Q(register_12_q), .clk(CLK), .clr(RESET));
  Register #(.width(32)) register_13 (
    .D(DATA_WRITE), .en(demultiplexer_1_out12), .Q(register_13_q), .clk(CLK), .clr(RESET));
  Register #(.width(32)) register_14 (
    .D(DATA_WRITE), .en(demultiplexer_1_out13), .Q(register_14_q), .clk(CLK), .clr(RESET));
  Register #(.width(32)) register_15 (
    .D(DATA_WRITE), .en(demultiplexer_1_out14), .Q(register_15_q), .clk(CLK), .clr(RESET));
  Register #(.width(32)) register_16 (
    .D(DATA_WRITE), .en(demultiplexer_1_out15), .Q(register_16_q), .clk(CLK), .clr(RESET));
  Multiplexer #(.select(4), .width(32), .disabled(0), .enable("false")) multiplexer_1 (
    .in0(register_1_q), .in1(register_2_q), .in2(register_3_q), .in3(register_4_q), .in4(register_5_q),
    .in5(register_6_q), .in6(register_7_q), .in7(register_8_q), .in8(register_9_q), .in9(register_10_q),
    .in10(register_11_q), .in11(register_12_q), .in12(register_13_q), .in13(register_14_q),
    .in14(register_15_q), .in15(register_16_q), .out(R0_D), .sel(R0));
  Multiplexer #(.select(4), .width(32), .enable("false")) multiplexer_2 (
    .in0(register_1_q), .in1(register_2_q), .in2(register_3_q), .in3(register_4_q), .in4(register_5_q),
    .in5(register_6_q), .in6(register_7_q), .in7(register_8_q), .in8(register_9_q), .in9(register_10_q),
    .in10(register_11_q), .in11(register_12_q), .in12(register_13_q), .in13(register_14_q),
    .in14(register_15_q), .in15(register_16_q), .out(R1_D), .sel(R1));
endmodule

module EXTENSOR_17_32 (
  input  [16:0] in_1,
  output [31:0] out_2
);

  assign out_2 = {{15{1'b0}}, in_1};  // Bit_Extender bit_extender_1
endmodule

module EXTENSOR_21_32 (
  input  [20:0] in_1,
  output [31:0] out_2
);

  assign out_2 = {{11{1'b0}}, in_1};  // Bit_Extender bit_extender_1
endmodule

module BOLHA (
  input  CLK,
  input  [31:0] INST,
  output out_3
);

  wire comparator_1_eq;

  Comparator #(.width(32), .mode("unsigned")) comparator_1 (
    .a({32{1'b0}}), .b(INST), .eq(comparator_1_eq));  // open: gt, lt
  and and_1 (out_3, CLK, ~comparator_1_eq);  // AND_Gate
endmodule

module ULA_END (
  input  [1:0] ENDC,
  input  EQUAL,
  output [1:0] END
);

  wire and_1_out, and_2_out;
  wire [1:0] multiplexer_2_out;

  Multiplexer #(.width(2)) multiplexer_1 (.in0(ENDC), .in1(multiplexer_2_out), .out(END), .sel(and_2_out));  // open: en
  Multiplexer #(.width(2)) multiplexer_2 (
    .in0(2'b00), .in1(2'b01), .out(multiplexer_2_out), .sel(and_1_out));  // open: en
  and and_1 (and_1_out, EQUAL, and_2_out);
  and and_2 (and_2_out, ENDC[0], ENDC[1]);
endmodule
